# Fritzing sketch salida audio sintetizador arduino (saved by Fritzing 0.9.2b)
breadboards: 1

parts:
  U4 = 3.5mm Audio Jack [package=audio-jack]
  R1 = Resistor [tolerance=±5% resistance=3.3k package=THT]
  C1 = Ceramic Capacitor [capacitance=10nF package="100 mil [THT, multilayer]"]
  C2 = Ceramic Capacitor [capacitance=10nF package="100 mil [THT, multilayer]"]
  R2 = Resistor [tolerance=±5% resistance=3.3k package=THT]

nets:
  N1: U4.RIGHT, R1.Pin_1, C2.1
  GND: U4.SLEEVE, C1.0, C2.0
  N2: U4.LEFT, C1.1, R2.Pin_1
  D9: R1.Pin_0, R2.Pin_0
