# Fritzing sketch sensores resistivos sintetizador arduino (saved by Fritzing 0.9.2b)
breadboards: 1

parts:
  R1 = Resistor [tolerance=±5% resistance=10M package=THT]
  R2 = Resistor [tolerance=±5% resistance=10M package=THT]
  Rn-1 = Resistor [tolerance=±5% resistance=10M package=THT]
  Rn = Resistor [tolerance=±5% resistance=10M package=THT]

nets:
  5V: R1.Pin_0, R2.Pin_0, Rn-1.Pin_0, Rn.Pin_0
  D12/Objeto 1: R1.Pin_1
  D11/Objeto 2: R2.Pin_1
  D3/Objeto n-1: Rn-1.Pin_1
  D2/Objeto n: Rn.Pin_1

notes:
  .
  Puede ser un brazalete
  o cualquier otra cosa
  que te conecte a tierra
  Objetos que conduzcan
  electricidad, aunque tengan
  resistencia elevada
